# Fritzing sketch NoiseGoblin (saved by Fritzing 1.0.5)

parts:
  M1 = ESP32-S3-DevKitC-1-N8R8-v1 [part_number=ESP32-S3-DevKitC-1-N8R8-v1]
  Part1 = Adafruit MAX98357A I2S 3W Class D Amplifier [part_number="Adafruit #3006"]
  SP1 = SPEAKER [package=pcb_mount_speaker]
  Reset = Pushbutton [package="[SMD]"]
  Play = Pushbutton [package="[SMD]"]

nets (from the schematic view):
  N1: M1.pin_1, M1.pin_2, Part1.VIN
  N2: M1.pin_4, M1.pin_5, M1.pin_22, M1.pin_44, Part1.GND, Reset.Pin_1, Reset.Pin_2, Play.Pin_1, Play.Pin_2
  N3: M1.pin_8, Part1.DIN
  N4: M1.pin_9, Part1.LRCLK
  N5: M1.pin_10, Part1.BCLK
  N6: Part1.VO-, SP1.+
  N7: Part1.VO+, SP1.-

custom parts:
  ESP32-S3-DevKitC-1-N8R8-v1: ESP32-S3-DevKitC-1-N8R8-v1 This module is 44pins long (2x22) and 11 pins width.
  Adafruit MAX98357A I2S 3W Class D Amplifier: Listen to this good news - we now have an all in one digital audio amp breakout board that works incredibly well with the Raspberry Pi! If you're looking for an easy and low cost way to get you digital sound files bumpin' then the MAX08357 I2S Amp Breakout is for you. It takes standard I2S digital audio input and, not only decodes it into analog, but also amplifies it directly into a speaker.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
